# Fritzing sketch frescobol-nano-bt (saved by Fritzing 0.9.3b)

parts:
  S1 = Momentary Switch [package=ksa_sealed_tac_switch]
  S2 = Momentary Switch [package=ksa_sealed_tac_switch]
  Part4 = Arduino Nano (Rev3.0) (ICSP)
  TP1 = TP4056 [chip_label=TP4056 package="DIP (Dual Inline) [THT]"]
  Part5 = Bluetooth HC-05 Macho
  J1 = male pin header, 2 pins [form="♂ (male)"]
  S3 = Momentary Switch [package=ksa_sealed_tac_switch]
  R1 = Resistor [tolerance=±5% resistance=2.2k package="0603 [SMD]"]
  R2 = Resistor [tolerance=±5% resistance=1k package="0603 [SMD]"]
  SW1 = DIP SWITCH [package=dipswitch-02]
  J2 = male pin header, 2 pins [form="♂ (male)"]

nets:
  N1: S1.2, Part4.D3
  N2: S1.3, J1.pin1
  N3: S1.4, S2.3, TP1.pin5
  N4: S2.2, Part4.D2
  GND: S2.4, Part4.GND, Part5.GND, S3.1, R1.Pin_0, J2.pin2
  N5: Part4.D1/TX, R2.Pin_0
  N6: Part4.D0/RX, Part5.TXD
  N7: Part4.D4, S3.4
  N8: Part4.D11/MOSI, J1.pin2
  N9: Part4.5V, SW1.1, SW1.2
  N10: TP1.pin4, SW1.3, J2.pin1
  N11: Part5.RXD, R1.Pin_1, R2.Pin_1
  N12: Part5.VCC, SW1.4

custom parts:
  TP4056: A DIP stand-in part for whatever IC you want. With 6 pins on a 300mil dual inline package (DIP) footprint.
